# Fritzing sketch rfid-arduino (saved by Fritzing 0.8.0b)
breadboards: 1
perfboards: 1

parts:
  Arduino1 = Arduino
  U1 = SM130 [package=sm130]  # not connected
  J3 = male pin header, 2 pins [form="♂ (male)"]  # not connected
  J2 = male pin header, 5 pins [form="♂ (male)"]
  J1 = single row smd male pin header, 5 pins [form="♂ (male)"]  # not connected

nets:
  N1: Arduino1.D4, J2.pin2
  N2: Arduino1.D3, J2.pin3
  N3: Arduino1.+5V, J2.pin5
  N4: Arduino1.GND, J2.pin1, J2.pin4
